# Fritzing sketch 5 sensor (saved by Fritzing 0.9.2b)
breadboards: 1

parts:
  TCRT1 = TCRT5000 sensor module [part_number=151608]
  TCRT2 = TCRT5000 sensor module [part_number=151608]
  TCRT3 = TCRT5000 sensor module [part_number=151608]
  TCRT4 = TCRT5000 sensor module [part_number=151608]
  TCRT5 = TCRT5000 sensor module [part_number=151608]
  Part1 = Arduino Uno (Rev3)
  R1 = Resistor [tolerance=±5% resistance=100 package="0805 [SMD]"]
  R2 = Resistor [tolerance=±5% resistance=100 package="0805 [SMD]"]
  R3 = Resistor [tolerance=±5% resistance=100 package="0805 [SMD]"]
  R4 = Resistor [tolerance=±5% resistance=100 package="0805 [SMD]"]
  R5 = Resistor [tolerance=±5% resistance=100 package="0805 [SMD]"]
  R6 = Resistor [tolerance=±5% resistance=10k package="0805 [SMD]"]
  R7 = Resistor [tolerance=±5% resistance=10k package="0805 [SMD]"]
  R8 = Resistor [tolerance=±5% resistance=10k package="0805 [SMD]"]
  R9 = Resistor [tolerance=±5% resistance=10k package="0805 [SMD]"]
  R10 = Resistor [tolerance=±5% resistance=10k package="0805 [SMD]"]

nets:
  N1: TCRT1.D+, TCRT1.T+, TCRT2.D+, TCRT2.T+, TCRT3.D+, TCRT3.T+, TCRT4.D+, TCRT4.T+, TCRT5.D+, TCRT5.T+, Part1.5V
  N2: TCRT1.D-, R1.Pin_1
  N3: TCRT1.T-, Part1.D3_PWM, R6.Pin_1
  N4: TCRT2.D-, R2.Pin_1
  N5: TCRT2.T-, Part1.D4, R7.Pin_1
  N6: TCRT3.D-, R3.Pin_1
  N7: TCRT3.T-, Part1.D5_PWM, R8.Pin_1
  N8: TCRT4.D-, R4.Pin_1
  N9: TCRT4.T-, Part1.D6_PWM, R9.Pin_1
  N10: TCRT5.D-, R5.Pin_1
  N11: TCRT5.T-, Part1.D7, R10.Pin_1
  N12: Part1.GND, R1.Pin_0, R2.Pin_0, R3.Pin_0, R4.Pin_0, R5.Pin_0, R6.Pin_0, R7.Pin_0, R8.Pin_0, R9.Pin_0, R10.Pin_0

custom parts:
  TCRT5000 sensor module: breakout board with TCRT5000
